# Fritzing sketch CENG317_PCB_DESIGN (saved by Fritzing 0.9.3b)
circuit board: 8.46667cm x 5.64444cm
breadboards: 1

parts:
  hc-sr1 = hc-sr04
  Arduino_Uno_(Rev3)_-_ICSP = Arduino Uno (Rev3) - ICSP
  DHT1 = Humidity and Temperature Sensor DHT11

nets:
  VCC: hc-sr1.VCC, Arduino_Uno_(Rev3)_-_ICSP.5V, DHT1.Vcc
  N1: hc-sr1.Trig, Arduino_Uno_(Rev3)_-_ICSP.ICSP_MOSI, Arduino_Uno_(Rev3)_-_ICSP.D11_PWM/MOSI
  N2: hc-sr1.Echo, Arduino_Uno_(Rev3)_-_ICSP.D12/MISO
  GND: hc-sr1.GND, Arduino_Uno_(Rev3)_-_ICSP.GND, DHT1.GND_1
  N3: Arduino_Uno_(Rev3)_-_ICSP.D7, DHT1.Data-signal

notes:
  Boswell Orendain

custom parts:
  Humidity and Temperature Sensor DHT11: Digital relative humidity & temperature sensor DHT11
